// Logisim project dijital24saat.circ as structural Verilog
module D10 (
  input  A,
  input  B,
  input  C,
  input  D,
  output DA,
  output DB,
  output DC,
  output DD,
  output R
);

  wire and_1_out, and_2_out, and_3_out, and_4_out, and_5_out, and_6_out, and_7_out, and_8_out, and_9_out,
       not_1_out, not_2_out, not_3_out, not_4_out;

  not not_1 (not_1_out, A);
  not not_2 (not_2_out, B);
  not not_3 (not_3_out, C);
  not not_4 (not_4_out, D);
  and and_1 (and_1_out, not_1_out, B, C, D);
  and and_2 (and_2_out, A, not_2_out, not_3_out, not_4_out);
  and and_3 (and_3_out, not_1_out, not_2_out, C, D);
  and and_4 (and_4_out, not_1_out, B, not_3_out);
  and and_5 (and_5_out, not_1_out, B, not_4_out);
  and and_6 (and_6_out, not_1_out, not_3_out, D);
  and and_7 (and_7_out, not_1_out, C, not_4_out);
  and and_8 (and_8_out, not_1_out, not_4_out);
  and and_9 (and_9_out, not_2_out, not_3_out, not_4_out);
  and and_10 (R, not_1_out, not_2_out, not_3_out, not_4_out);
  or or_1 (DA, and_1_out, and_2_out);
  or or_2 (DB, and_3_out, and_4_out, and_5_out);
  or or_3 (DC, and_6_out, and_7_out);
  or or_4 (DD, and_8_out, and_9_out);
endmodule

module DD10 (
  input  CLK,
  output [3:0] O,
  output R
);

  wire d10_1_da, d10_1_db, d10_1_dc, d10_1_dd;

  D10 d10_1 (.A(O[3]), .B(O[2]), .C(O[1]), .D(O[0]), .DA(d10_1_da), .DB(d10_1_db), .DC(d10_1_dc), .DD(d10_1_dd), .R(R));
  D_Flip_Flop d_ff_1 (.D(d10_1_da), .clk(CLK), .Q(O[3]));  // open: Qn, preset, reset
  D_Flip_Flop d_ff_2 (.D(d10_1_db), .clk(CLK), .Q(O[2]));  // open: Qn, preset, reset
  D_Flip_Flop d_ff_3 (.D(d10_1_dc), .clk(CLK), .Q(O[1]));  // open: Qn, preset, reset
  D_Flip_Flop d_ff_4 (.D(d10_1_dd), .clk(CLK), .Q(O[0]));  // open: Qn, preset, reset
endmodule

module DD6 (
  input  CLK,
  output [3:0] O,
  output R
);

  wire d6_1_da, d6_1_db, d6_1_dc;

  D_Flip_Flop d_ff_1 (.D(d6_1_da), .clk(CLK), .Q(O[2]));  // open: Qn, preset, reset
  D6 d6_1 (.A(O[2]), .B(O[1]), .C(O[0]), .DA(d6_1_da), .DB(d6_1_db), .DC(d6_1_dc), .R(R));
  D_Flip_Flop d_ff_2 (.D(d6_1_db), .clk(CLK), .Q(O[1]));  // open: Qn, preset, reset
  D_Flip_Flop d_ff_3 (.D(d6_1_dc), .clk(CLK), .Q(O[0]));  // open: Qn, preset, reset

  assign O[3] = 1'b0;
endmodule

module D6 (
  input  A,
  input  B,
  input  C,
  output DA,
  output DB,
  output DC,
  output R
);

  wire and_1_out, and_2_out, and_3_out, and_4_out, and_5_out, and_6_out, not_1_out, not_2_out, not_3_out;

  not not_1 (not_1_out, A);
  not not_2 (not_2_out, B);
  not not_3 (not_3_out, C);
  and and_1 (and_1_out, not_1_out, B, C);
  or or_1 (DA, and_1_out, and_2_out);
  and and_2 (and_2_out, A, not_2_out, not_3_out);
  and and_3 (and_3_out, not_1_out, not_2_out, C);
  or or_2 (DB, and_3_out, and_4_out);
  and and_4 (and_4_out, not_1_out, B, not_3_out);
  and and_5 (and_5_out, not_1_out, not_3_out);
  or or_3 (DC, and_5_out, and_6_out);
  and and_6 (and_6_out, not_2_out, not_3_out);
  and and_7 (R, not_1_out, not_2_out, not_3_out);
endmodule

module DD3 (
  input  CLK,
  output [3:0] out_2,
  output R
);

  wire d3_1_da, d3_1_db;

  D3 d3_1 (.A(out_2[1]), .B(out_2[0]), .DA(d3_1_da), .DB(d3_1_db), .R(R));
  D_Flip_Flop d_ff_1 (.D(d3_1_da), .clk(CLK), .Q(out_2[1]));  // open: Qn, preset, reset
  D_Flip_Flop d_ff_2 (.D(d3_1_db), .clk(CLK), .Q(out_2[0]));  // open: Qn, preset, reset

  assign out_2[3:2] = 2'b00;
endmodule

module D3 (
  input  A,
  input  B,
  output DA,
  output DB,
  output R
);

  wire not_1_out, not_2_out;

  not not_1 (not_1_out, A);
  not not_2 (not_2_out, B);
  and and_1 (DA, not_1_out, B);
  and and_2 (DB, not_1_out, not_2_out);
  and and_3 (R, not_1_out, not_2_out);
endmodule

module DD24 (
  input  A,
  input  B,
  input  C,
  input  D,
  input  [3:0] H10,
  output DA,
  output DB,
  output DC,
  output DD,
  output R
);

  wire and_1_out, not_1_out;
  wire [4:0] d10_1_da;

  not not_1 (not_1_out, H10[0]);
  D10 d10_1 (
    .A(A), .B(B), .C(C), .D(D), .DA(d10_1_da[0]), .DB(d10_1_da[1]), .DC(d10_1_da[2]), .DD(d10_1_da[3]),
    .R(d10_1_da[4]));
  and and_1 (and_1_out, C, D, not_1_out, H10[1]);
  Multiplexer #(.disabled("Z"), .enable("true"), .width(5)) multiplexer_1 (
    .in0(d10_1_da), .in1({d10_1_da[4], 4'b0000}), .out({R, DD, DC, DB, DA}), .sel(and_1_out));  // open: en
endmodule

module D24 (
  input  [3:0] H10,
  input  CLK,
  output [3:0] O,
  output R
);

  wire dd24_1_da, dd24_1_db, dd24_1_dc, dd24_1_dd;

  DD24 dd24_1 (
    .A(O[3]), .B(O[2]), .C(O[1]), .D(O[0]), .H10(H10), .DA(dd24_1_da), .DB(dd24_1_db), .DC(dd24_1_dc),
    .DD(dd24_1_dd), .R(R));
  D_Flip_Flop d_ff_1 (.D(dd24_1_da), .clk(CLK), .Q(O[3]));  // open: Qn, preset, reset
  D_Flip_Flop d_ff_2 (.D(dd24_1_db), .clk(CLK), .Q(O[2]));  // open: Qn, preset, reset
  D_Flip_Flop d_ff_3 (.D(dd24_1_dc), .clk(CLK), .Q(O[1]));  // open: Qn, preset, reset
  D_Flip_Flop d_ff_4 (.D(dd24_1_dd), .clk(CLK), .Q(O[0]));  // open: Qn, preset, reset
endmodule

module SAAT24 (
);

  wire clock_1_out, d24_1_r, dd6_1_r, dd6_2_r, dd10_1_r, dd10_2_r;
  wire [3:0] d24_1_o, dd3_1_out_2, dd6_1_o, dd6_2_o, dd10_1_o, dd10_2_o;

  Hex_Digit_Display hex_digit_display_1 (.value(dd3_1_out_2));  // open: dp
  Hex_Digit_Display hex_digit_display_2 (.value(d24_1_o));  // open: dp
  DD3 dd3_1 (.CLK(d24_1_r), .out_2(dd3_1_out_2));  // open: R
  D24 d24_1 (.H10(dd3_1_out_2), .CLK(dd6_1_r), .O(d24_1_o), .R(d24_1_r));
  Hex_Digit_Display hex_digit_display_3 (.value(dd6_1_o));  // open: dp
  Hex_Digit_Display hex_digit_display_4 (.value(dd10_1_o));  // open: dp
  Hex_Digit_Display hex_digit_display_5 (.value(dd6_2_o));  // open: dp
  Hex_Digit_Display hex_digit_display_6 (.value(dd10_2_o));  // open: dp
  DD10 dd10_1 (.CLK(dd6_2_r), .O(dd10_1_o), .R(dd10_1_r));
  DD6 dd6_1 (.CLK(dd10_1_r), .O(dd6_1_o), .R(dd6_1_r));
  Clock clock_1 (.out(clock_1_out));
  DD6 dd6_2 (.CLK(dd10_2_r), .O(dd6_2_o), .R(dd6_2_r));
  DD10 dd10_2 (.CLK(clock_1_out), .O(dd10_2_o), .R(dd10_2_r));
endmodule
